# Fritzing sketch Unicorn-Circuit (saved by Fritzing 0.7.11b)
breadboards: 1

parts:
  Q1 = NPN-Transistor [package="TO92 [THT]"]  # not connected
  VCC1 = Battery block 9V
  Arduino1 = Arduino Nano v3.0

nets:
  N1: VCC1.-, Arduino1.GND
  N2: VCC1.+, Arduino1.VIN
